# Fritzing sketch Untitled Sketch (saved by Fritzing 0.9.3b)
breadboards: 1

parts:
  元件1 = Arduino Uno (Rev3)
  Raspberry_Pi_1 = Raspberry Pi 3 [part_number=RPI-3-V1.2]  # not connected
  元件2 = Soil Moisture Sensor
  DS1 = DS18B20 1-Wire Temperature Sensor [part_number=DS18B20]

nets:
  N1: 元件1.A0, 元件2.SIG
  N2: 元件1.A1, DS1.DQ
  N3: 元件1.D7, 元件2.VCC
  5V: 元件1.5V, DS1.VDD
  GND: 元件1.GND, 元件2.GND, DS1.GND
