# Fritzing sketch pi (saved by Fritzing 0.9.3b)
breadboards: 1

parts:
  IC1 = MCP3008 8-channel 10-bit ADC [part_number=MCP3008]
  T1 = TMP36 Temperature Sensor [package="TO92 [THT]"]
  元件1 = Soil Moisture Sensor
  Raspberry_Pi_1 = Raspberry Pi 3 [part_number=RPI-3-V1.2]

nets:
  N1: IC1.no_name_yet#1, T1.Vout
  N2: IC1.no_name_yet#2, 元件1.SIG
  GND: IC1.no_name_yet#9, IC1.no_name_yet#14, T1.GND, 元件1.GND, Raspberry_Pi_1.GND
  N3: IC1.no_name_yet#10, Raspberry_Pi_1.GIPO8
  N4: IC1.no_name_yet#11, Raspberry_Pi_1.GIPO10
  N5: IC1.no_name_yet#12, Raspberry_Pi_1.GIPO9
  N6: IC1.no_name_yet#13, Raspberry_Pi_1.GIPO11
  N7: IC1.no_name_yet#15, IC1.no_name_yet#16, T1.+Vs, Raspberry_Pi_1.3v3
  VCC: 元件1.VCC, Raspberry_Pi_1.5V

notes:
  By Rui Melo Aka ViPeR5000
